# Fritzing sketch board (saved by Fritzing 0.9.3b)
breadboards: 1

parts:
  Raspberry_Pi_1 = Raspberry Pi 3 [part_number=RPI-3-V1.2]
  J1 = Piezo Speaker
  J2 = Piezo Speaker
  R1 = Trimmer Potentiometer [maximum_resistance=10kΩ package=THT]
  R2 = Resistor [tolerance=±5% resistance=200 package=THT]
  Q1 = MOSFET-NCHANNEL [package=to220v]
  R3 = Resistor [tolerance=±5% resistance=200 package=THT]
  Q2 = MOSFET-NCHANNEL [package=to220v]
  R4 = Resistor [tolerance=±5% resistance=200 package=THT]
  J3 = Piezo Speaker
  Q3 = MOSFET-NCHANNEL [package=to220v]
  R5 = Resistor [tolerance=±5% resistance=200 package=THT]
  J4 = Piezo Speaker
  Q4 = MOSFET-NCHANNEL [package=to220v]
  R6 = Resistor [tolerance=±5% resistance=200 package=THT]
  J5 = Piezo Speaker
  Q5 = MOSFET-NCHANNEL [package=to220v]
  R7 = Resistor [tolerance=±5% resistance=200 package=THT]
  J6 = Piezo Speaker
  Q6 = MOSFET-NCHANNEL [package=to220v]
  R8 = Resistor [tolerance=±5% resistance=200 package=THT]
  Q7 = MOSFET-NCHANNEL [package=to220v]
  J7 = Piezo Speaker
  R9 = Resistor [tolerance=±5% resistance=200 package=THT]
  J8 = Piezo Speaker
  Q8 = MOSFET-NCHANNEL [package=to220v]

nets:
  3V3: Raspberry_Pi_1.3v3, Raspberry_Pi_1.3V3
  N1: Raspberry_Pi_1.GND, J1.pin2, J2.pin2, J3.pin2, J4.pin2, J5.pin1, J6.pin1, J7.pin1, J8.pin1
  N2: Raspberry_Pi_1.GPIO27, R6.Pin_0
  N3: Raspberry_Pi_1.GPIO22, R7.Pin_0
  N4: Raspberry_Pi_1.GPIO5, R8.Pin_0
  N5: Raspberry_Pi_1.GPIO13, R9.Pin_0
  N6: Raspberry_Pi_1.GPIO12, R5.Pin_0
  N7: Raspberry_Pi_1.GPIO25, R4.Pin_0
  N8: Raspberry_Pi_1.GPIO23, R3.Pin_0
  N9: Raspberry_Pi_1.GPIO18, R2.Pin_0
  N10: Raspberry_Pi_1.5V, R1.leg1, R1.wiper
  N11: J1.pin1, Q1.S
  N12: J2.pin1, Q2.S
  N13: R1.leg2, Q1.G, Q2.G, Q3.G, Q4.G, Q5.G, Q6.G, Q7.G, Q8.G
  N14: R2.Pin_1, Q1.D
  N15: R3.Pin_1, Q2.D
  N16: R4.Pin_1, Q3.D
  N17: J3.pin1, Q3.S
  N18: R5.Pin_1, Q4.D
  N19: J4.pin1, Q4.S
  N20: R6.Pin_1, Q5.D
  N21: J5.pin2, Q5.S
  N22: R7.Pin_1, Q6.D
  N23: J6.pin2, Q6.S
  N24: R8.Pin_1, Q7.D
  N25: Q7.S, J7.pin2
  N26: R9.Pin_1, Q8.D
  N27: J8.pin2, Q8.S
