# Fritzing sketch unit (saved by Fritzing 0.9.3b)
breadboards: 1

parts:
  GPIO = Toggle Switch [package=THT]
  2N7000 = Basic FET N-Channel [package="TO220 [THT]"]
  R1 = Resistor [tolerance=±5% resistance=200 package=THT]
  パッシブブザー = Buzzer 12mm [package=buzzer-ccv-kit]
  ボリューム調節 = Basic Flex Resistor

nets:
  3.3V: GPIO.L1
  N1: GPIO.COM, R1.Pin_0
  GND: GPIO.L2, パッシブブザー.2
  N2: 2N7000.gate, R1.Pin_1
  N3: 2N7000.drain, ボリューム調節.Pin_2
  N4: 2N7000.source, パッシブブザー.1
  5V: ボリューム調節.pin_1
